// Logisim project Compu.circ as structural Verilog: 2 circuits, main circuit main
module main (
  input  [7:0] in_1
);

  wire and_1_out, and_3_out, and_4_out, and_5_out, clock_1_out, clock_2_out, comparator_1_eq,
       comparator_1_gt, comparator_1_lt, comparator_2_eq, comparator_3_eq, comparator_4_eq, comparator_5_eq,
       CONDITION_q, counter_1_q, d_ff_1_q, d_ff_2_q, demultiplexer_1_out0, demultiplexer_1_out1,
       demultiplexer_1_out2, demultiplexer_1_out3, demultiplexer_1_out4, demultiplexer_1_out5,
       demultiplexer_1_out6, demultiplexer_1_out7, demultiplexer_1_out8, demultiplexer_1_out9,
       demultiplexer_1_out10, demultiplexer_1_out11, demultiplexer_1_out12, demultiplexer_1_out13,
       demultiplexer_1_out14, demultiplexer_1_out15, demultiplexer_1_out16, demultiplexer_1_out17,
       demultiplexer_1_out18, demultiplexer_1_out19, Frame_Ready_out, not_1_out, not_2_out, not_3_out,
       not_4_out, not_5_out, ram_load_read_controller_1_load, ram_load_read_controller_1_store,
       ram_load_read_controller_2_load, ram_load_read_controller_2_store, ram_load_read_controller_3_load,
       ram_load_read_controller_3_store, ram_load_read_controller_4_load, ram_load_read_controller_4_store,
       register_1_q, RESET_out, s_r_ff_1_q;
  wire [1:0] PC_JUMP_OP_q;
  wire [3:0] ALU_OP_q, binary_to_bcd_converter_1_p2, binary_to_bcd_converter_1_p3,
       binary_to_bcd_converter_1_p4, binary_to_bcd_converter_2_p2, binary_to_bcd_converter_2_p3,
       binary_to_bcd_converter_2_p4, binary_to_bcd_converter_3_p1, binary_to_bcd_converter_3_p3,
       binary_to_bcd_converter_3_p4, binary_to_bcd_converter_3_p5, binary_to_bcd_converter_4_p1,
       binary_to_bcd_converter_4_p3, binary_to_bcd_converter_4_p4, binary_to_bcd_converter_4_p5,
       binary_to_bcd_converter_5_p1, binary_to_bcd_converter_5_p3, binary_to_bcd_converter_5_p4,
       binary_to_bcd_converter_5_p5, binary_to_bcd_converter_5_p6, binary_to_bcd_converter_6_p1,
       binary_to_bcd_converter_6_p3, binary_to_bcd_converter_6_p4, binary_to_bcd_converter_6_p5,
       binary_to_bcd_converter_6_p6, binary_to_bcd_converter_7_p2, binary_to_bcd_converter_7_p3,
       binary_to_bcd_converter_7_p4, binary_to_bcd_converter_8_p1, binary_to_bcd_converter_8_p3,
       binary_to_bcd_converter_8_p4, binary_to_bcd_converter_8_p5, binary_to_bcd_converter_9_p1,
       binary_to_bcd_converter_9_p3, binary_to_bcd_converter_9_p4, binary_to_bcd_converter_9_p5,
       binary_to_bcd_converter_9_p6;
  wire [9:0] GPU_INS_ADR_q, GPU_PC_q_2, multiplexer_1_out, multiplexer_1_out_2, multiplexer_4_out;
  wire [10:0] GPU_PC_q;
  wire [11:0] binary_to_bcd_converter_2_p1, multiplexer_1_out_3;
  wire [19:0] ALU_X_q;
  wire [23:0] ColorPalette_data, demultiplexer_3_out0, demultiplexer_3_out1, END_DIR_q, FrameBuffer0_dout,
       FrameBuffer1_dout, multiplexer_2_out, multiplexer_3_out, multiplexer_5_out, PC_q, rgb_video_1_p6,
       STACK_PC_ADR_q, STACK_PC_dout, START_DIR_q;
  wire [31:0] adder_1_out, ALU_Y_q, and_2_out, bit_extender_1_out, bit_extender_2_out, bit_extender_3_out,
       divider_1_out, Instructions_data, multiplier_1_out, nand_1_out, nor_1_out, or_1_out, R0_q, R1_q, R2_q,
       R3_q, R4_q, R5_q, R6_q, R7_q, subtractor_1_out, xnor_1_out, xor_1_out;
  wire [31:24] multiplexer_2_out_2;
  wire [41:32] Instructions_data_2;

  Clock clock_1 (.out(clock_1_out));
  Button RESET (.out(RESET_out));
  Hex_Digit_Display hex_digit_display_1 (.value(binary_to_bcd_converter_1_p2));  // open: dp
  // Binary_to_BCD_converter #(.binvalue(12)) binary_to_bcd_converter_1: pin names not known; wires that end beside it: ALU_Y_q[31:20], binary_to_bcd_converter_1_p2, binary_to_bcd_converter_1_p3, binary_to_bcd_converter_1_p4
  Hex_Digit_Display hex_digit_display_2 (.value(binary_to_bcd_converter_2_p2));  // open: dp
  // Binary_to_BCD_converter #(.binvalue(12)) binary_to_bcd_converter_2: pin names not known; wires that end beside it: binary_to_bcd_converter_2_p1, binary_to_bcd_converter_2_p2, binary_to_bcd_converter_2_p3, binary_to_bcd_converter_2_p4
  D_Flip_Flop d_ff_1 (.D(RESET_out), .clk(clock_1_out), .Q(d_ff_1_q));  // open: Qn, preset, reset
  Hex_Digit_Display hex_digit_display_3 (.value(binary_to_bcd_converter_1_p3));  // open: dp
  Hex_Digit_Display hex_digit_display_4 (.value(binary_to_bcd_converter_1_p4));  // open: dp
  Hex_Digit_Display hex_digit_display_5 (.value(binary_to_bcd_converter_2_p3));  // open: dp
  Hex_Digit_Display hex_digit_display_6 (.value(binary_to_bcd_converter_2_p4));  // open: dp
  Register #(.width(32)) ALU_X (
    .D({multiplexer_2_out_2, multiplexer_2_out}), .en(demultiplexer_1_out0), .clk(clock_1_out),
    .Q({binary_to_bcd_converter_2_p1, ALU_X_q}), .clr(and_1_out));
  Register #(.width(32)) ALU_Y (
    .D({multiplexer_2_out_2, multiplexer_2_out}), .en(demultiplexer_1_out1), .clk(clock_1_out), .Q(ALU_Y_q),
    .clr(and_1_out));
  not not_1 (not_1_out, d_ff_1_q);
  Hex_Digit_Display hex_digit_display_7 (.value(binary_to_bcd_converter_3_p1));  // open: dp
  Hex_Digit_Display hex_digit_display_8 (.value(binary_to_bcd_converter_4_p1));  // open: dp
  and and_1 (and_1_out, RESET_out, not_1_out);
  Hex_Digit_Display hex_digit_display_9 (.value(binary_to_bcd_converter_3_p3));  // open: dp
  // Binary_to_BCD_converter #(.binvalue(10)) binary_to_bcd_converter_3: pin names not known; wires that end beside it: binary_to_bcd_converter_3_p1, ALU_Y_q[19:10], binary_to_bcd_converter_3_p3, binary_to_bcd_converter_3_p4, binary_to_bcd_converter_3_p5
  Hex_Digit_Display hex_digit_display_10 (.value(binary_to_bcd_converter_4_p3));  // open: dp
  // Binary_to_BCD_converter #(.binvalue(10)) binary_to_bcd_converter_4: pin names not known; wires that end beside it: binary_to_bcd_converter_4_p1, ALU_X_q[19:10], binary_to_bcd_converter_4_p3, binary_to_bcd_converter_4_p4, binary_to_bcd_converter_4_p5
  Adder #(.width(32)) adder_1 (
    .a({binary_to_bcd_converter_2_p1, ALU_X_q}), .b(ALU_Y_q), .out(adder_1_out));  // open: cin, cout
  Subtractor #(.width(32)) subtractor_1 (
    .a({binary_to_bcd_converter_2_p1, ALU_X_q}), .b(ALU_Y_q), .out(subtractor_1_out));  // open: bin, bout
  Multiplier #(.width(32)) multiplier_1 (
    .a({binary_to_bcd_converter_2_p1, ALU_X_q}), .b(ALU_Y_q), .out(multiplier_1_out));  // open: cin, cout
  Divider #(.width(32)) divider_1 (
    .a({binary_to_bcd_converter_2_p1, ALU_X_q}), .b(ALU_Y_q), .out(divider_1_out));  // open: upper, rem
  assign and_2_out = {binary_to_bcd_converter_2_p1, ALU_X_q} & ALU_Y_q;  // AND_Gate and_2, 32 bits wide
  assign nand_1_out = ~({binary_to_bcd_converter_2_p1, ALU_X_q} & ALU_Y_q);  // NAND_Gate nand_1, 32 bits wide
  assign or_1_out = {binary_to_bcd_converter_2_p1, ALU_X_q} | ALU_Y_q;  // OR_Gate or_1, 32 bits wide
  assign nor_1_out = ~({binary_to_bcd_converter_2_p1, ALU_X_q} | ALU_Y_q);  // NOR_Gate nor_1, 32 bits wide
  assign xor_1_out = {binary_to_bcd_converter_2_p1, ALU_X_q} ^ ALU_Y_q;  // XOR_Gate xor_1, 32 bits wide
  assign xnor_1_out = ~({binary_to_bcd_converter_2_p1, ALU_X_q} ^ ALU_Y_q);  // XNOR_Gate xnor_1, 32 bits wide
  assign bit_extender_1_out = {{31{1'b0}}, comparator_1_gt};  // Bit_Extender bit_extender_1
  assign bit_extender_2_out = {{31{1'b0}}, comparator_1_eq};  // Bit_Extender bit_extender_2
  Comparator #(.mode("unsigned"), .width(32)) comparator_1 (
    .a({binary_to_bcd_converter_2_p1, ALU_X_q}), .b(ALU_Y_q), .gt(comparator_1_gt), .eq(comparator_1_eq),
    .lt(comparator_1_lt));
  assign bit_extender_3_out = {{31{1'b0}}, comparator_1_lt};  // Bit_Extender bit_extender_3
  Hex_Digit_Display hex_digit_display_11 (.value(binary_to_bcd_converter_3_p4));  // open: dp
  Hex_Digit_Display hex_digit_display_12 (.value(binary_to_bcd_converter_4_p4));  // open: dp
  Register #(.width(4)) ALU_OP (
    .D(multiplexer_2_out[3:0]), .en(demultiplexer_1_out16), .clk(clock_1_out), .Q(ALU_OP_q), .clr(and_1_out));
  Hex_Digit_Display hex_digit_display_13 (.value(binary_to_bcd_converter_3_p5));  // open: dp
  Hex_Digit_Display hex_digit_display_14 (.value(binary_to_bcd_converter_5_p1));  // open: dp
  Hex_Digit_Display hex_digit_display_15 (.value(binary_to_bcd_converter_4_p5));  // open: dp
  Hex_Digit_Display hex_digit_display_16 (.value(binary_to_bcd_converter_6_p1));  // open: dp
  Demultiplexer #(.select(5)) demultiplexer_1 (
    .out0(demultiplexer_1_out0), .out1(demultiplexer_1_out1), .out2(demultiplexer_1_out2),
    .out3(demultiplexer_1_out3), .out4(demultiplexer_1_out4), .out5(demultiplexer_1_out5),
    .out6(demultiplexer_1_out6), .out7(demultiplexer_1_out7), .out8(demultiplexer_1_out8),
    .out9(demultiplexer_1_out9), .out10(demultiplexer_1_out10), .out11(demultiplexer_1_out11),
    .out12(demultiplexer_1_out12), .out13(demultiplexer_1_out13), .out14(demultiplexer_1_out14),
    .out15(demultiplexer_1_out15), .out16(demultiplexer_1_out16), .out17(demultiplexer_1_out17),
    .out18(demultiplexer_1_out18), .out19(demultiplexer_1_out19), .in(Instructions_data_2[36]),
    .sel(Instructions_data_2[41:37]));  // open: out20, out21, out22, out23, out24, out25, out26, out27, out28, out29, out30, out31
  Register #(.width(1)) register_1 (.D(not_2_out), .en(1'b1), .clk(clock_1_out), .Q(register_1_q), .clr(and_1_out));
  Hex_Digit_Display hex_digit_display_17 (.value(binary_to_bcd_converter_5_p3));  // open: dp
  // Binary_to_BCD_converter #(.binvalue(10)) binary_to_bcd_converter_5: pin names not known; wires that end beside it: binary_to_bcd_converter_5_p1, ALU_Y_q[9:0], binary_to_bcd_converter_5_p3, binary_to_bcd_converter_5_p4, binary_to_bcd_converter_5_p5, binary_to_bcd_converter_5_p6
  Hex_Digit_Display hex_digit_display_18 (.value(binary_to_bcd_converter_6_p3));  // open: dp
  // Binary_to_BCD_converter #(.binvalue(10)) binary_to_bcd_converter_6: pin names not known; wires that end beside it: binary_to_bcd_converter_6_p1, ALU_X_q[9:0], binary_to_bcd_converter_6_p3, binary_to_bcd_converter_6_p4, binary_to_bcd_converter_6_p5, binary_to_bcd_converter_6_p6
  Multiplexer #(.select(4), .width(32)) multiplexer_1 (
    .in0(adder_1_out), .in1(subtractor_1_out), .in2(multiplier_1_out), .in3(divider_1_out), .in4(and_2_out),
    .in5(nand_1_out), .in6(or_1_out), .in7(nor_1_out), .in8(xor_1_out), .in9(xnor_1_out),
    .in10(bit_extender_1_out), .in11(bit_extender_2_out), .in12(bit_extender_3_out),
    .out({multiplexer_1_out_3, multiplexer_1_out_2, multiplexer_1_out}), .sel(ALU_OP_q));  // open: in13, in14, in15
  Comparator #(.mode("unsigned"), .width(1)) comparator_2 (
    .a(register_1_q), .b(1'b1), .eq(comparator_2_eq));  // open: gt, lt
  not not_2 (not_2_out, register_1_q);
  not not_3 (not_3_out, comparator_3_eq);
  Comparator #(.mode("unsigned"), .width(1)) comparator_3 (.a(1'b0), .b(1'b1), .eq(comparator_3_eq));  // open: gt, lt
  Hex_Digit_Display hex_digit_display_19 (.value(binary_to_bcd_converter_5_p4));  // open: dp
  Hex_Digit_Display hex_digit_display_20 (.value(binary_to_bcd_converter_6_p4));  // open: dp
  Register #(.width(32)) R0 (
    .D({multiplexer_2_out_2, multiplexer_2_out}), .en(demultiplexer_1_out2), .clk(clock_1_out), .Q(R0_q),
    .clr(and_1_out));
  and and_3 (and_3_out, comparator_2_eq, not_3_out);
  Hex_Digit_Display hex_digit_display_21 (.value(binary_to_bcd_converter_5_p5));  // open: dp
  Hex_Digit_Display hex_digit_display_22 (.value(binary_to_bcd_converter_6_p5));  // open: dp
  ROM #(.addrWidth(24), .dataWidth(42)) Instructions (.addr(PC_q), .data({Instructions_data_2, Instructions_data}));
  Counter #(.max('hffffff), .width(24)) PC (
    .load(demultiplexer_1_out15), .D(multiplexer_5_out), .count(and_3_out), .Q(PC_q), .up(1'b1),
    .clk(clock_1_out), .clr(and_1_out));  // open: carry
  Hex_Digit_Display hex_digit_display_23 (.value(binary_to_bcd_converter_5_p6));  // open: dp
  Hex_Digit_Display hex_digit_display_24 (.value(binary_to_bcd_converter_6_p6));  // open: dp
  Register #(.width(32)) R1 (
    .D({multiplexer_2_out_2, multiplexer_2_out}), .en(demultiplexer_1_out3), .clk(clock_1_out), .Q(R1_q),
    .clr(and_1_out));
  Hex_Digit_Display hex_digit_display_25 (.value(binary_to_bcd_converter_7_p2));  // open: dp
  // Binary_to_BCD_converter #(.binvalue(12)) binary_to_bcd_converter_7: pin names not known; wires that end beside it: multiplexer_1_out_3, binary_to_bcd_converter_7_p2, binary_to_bcd_converter_7_p3, binary_to_bcd_converter_7_p4
  Register #(.width(32)) R2 (
    .D({multiplexer_2_out_2, multiplexer_2_out}), .en(demultiplexer_1_out4), .clk(clock_1_out), .Q(R2_q),
    .clr(and_1_out));
  Hex_Digit_Display hex_digit_display_26 (.value(binary_to_bcd_converter_7_p3));  // open: dp
  Register #(.width(32)) R3 (
    .D({multiplexer_2_out_2, multiplexer_2_out}), .en(demultiplexer_1_out5), .clk(clock_1_out), .Q(R3_q),
    .clr(and_1_out));
  Register #(.width(24)) STACK_PC_ADR (
    .D(multiplexer_2_out), .en(demultiplexer_1_out19), .clk(and_3_out), .Q(STACK_PC_ADR_q), .clr(and_1_out));
  Hex_Digit_Display hex_digit_display_27 (.value(binary_to_bcd_converter_7_p4));  // open: dp
  Hex_Digit_Display hex_digit_display_28 (.value(binary_to_bcd_converter_8_p1));  // open: dp
  RAM_LOAD_READ_CONTROLLER ram_load_read_controller_1 (
    .STORE_SIGNAL(demultiplexer_1_out14), .LOAD(ram_load_read_controller_1_load),
    .STORE(ram_load_read_controller_1_store));
  Hex_Digit_Display hex_digit_display_29 (.value(binary_to_bcd_converter_8_p3));  // open: dp
  // Binary_to_BCD_converter #(.binvalue(10)) binary_to_bcd_converter_8: pin names not known; wires that end beside it: binary_to_bcd_converter_8_p1, multiplexer_1_out_2, binary_to_bcd_converter_8_p3, binary_to_bcd_converter_8_p4, binary_to_bcd_converter_8_p5
  Register #(.width(32)) R4 (
    .D({multiplexer_2_out_2, multiplexer_2_out}), .en(demultiplexer_1_out6), .clk(clock_1_out), .Q(R4_q),
    .clr(and_1_out));
  RAM #(.addrWidth(24), .dataWidth(24)) STACK_PC (
    .addr(STACK_PC_ADR_q), .we(ram_load_read_controller_1_store), .oe(ram_load_read_controller_1_load),
    .clk(and_3_out), .din(multiplexer_2_out), .dout(STACK_PC_dout));
  Hex_Digit_Display hex_digit_display_30 (.value(binary_to_bcd_converter_8_p4));  // open: dp
  Register #(.width(32)) R5 (
    .D({multiplexer_2_out_2, multiplexer_2_out}), .en(demultiplexer_1_out7), .clk(clock_1_out), .Q(R5_q),
    .clr(and_1_out));
  Hex_Digit_Display hex_digit_display_31 (.value(binary_to_bcd_converter_8_p5));  // open: dp
  Multiplexer #(.select(4), .width(32)) multiplexer_2 (
    .in0({multiplexer_1_out_3, multiplexer_1_out_2, multiplexer_1_out}), .in1(R0_q), .in2(R1_q), .in3(R2_q),
    .in4(R3_q), .in5(R4_q), .in6(R5_q), .in7(R6_q), .in8(R7_q), .in9(Instructions_data),
    .out({multiplexer_2_out_2, multiplexer_2_out}), .sel(Instructions_data_2[35:32]));  // open: in10, in11, in12, in13, in14, in15
  Register #(.width(1)) CONDITION (
    .D(multiplexer_2_out[0]), .en(demultiplexer_1_out11), .clk(clock_1_out), .Q(CONDITION_q), .clr(and_1_out));
  Register #(.width(24)) START_DIR (
    .D(multiplexer_2_out), .en(demultiplexer_1_out12), .clk(clock_1_out), .Q(START_DIR_q), .clr(and_1_out));
  Register #(.width(24)) END_DIR (
    .D(multiplexer_2_out), .en(demultiplexer_1_out13), .clk(clock_1_out), .Q(END_DIR_q), .clr(and_1_out));
  Hex_Digit_Display hex_digit_display_32 (.value(binary_to_bcd_converter_9_p1));  // open: dp
  Register #(.width(10)) GPU_INS_ADR (
    .D(multiplexer_2_out[9:0]), .en(demultiplexer_1_out18), .clk(clock_2_out), .Q(GPU_INS_ADR_q),
    .clr(and_1_out));
  Register #(.width(32)) R6 (
    .D({multiplexer_2_out_2, multiplexer_2_out}), .en(demultiplexer_1_out8), .clk(clock_1_out), .Q(R6_q),
    .clr(and_1_out));
  Comparator #(.width(1)) comparator_4 (.a(CONDITION_q), .b(1'b1), .eq(comparator_4_eq));  // open: gt, lt
  Hex_Digit_Display hex_digit_display_33 (.value(binary_to_bcd_converter_9_p3));  // open: dp
  Hex_Digit_Display hex_digit_display_34 (.value(binary_to_bcd_converter_9_p4));  // open: dp
  // Binary_to_BCD_converter #(.binvalue(10)) binary_to_bcd_converter_9: pin names not known; wires that end beside it: binary_to_bcd_converter_9_p1, multiplexer_1_out, binary_to_bcd_converter_9_p3, binary_to_bcd_converter_9_p4, binary_to_bcd_converter_9_p5, binary_to_bcd_converter_9_p6
  Register #(.width(32)) R7 (
    .D({multiplexer_2_out_2, multiplexer_2_out}), .en(demultiplexer_1_out9), .clk(clock_1_out), .Q(R7_q),
    .clr(and_1_out));
  Register #(.width(2)) PC_JUMP_OP (
    .D({multiplexer_2_out[2], multiplexer_2_out[0]}), .en(demultiplexer_1_out17), .clk(clock_1_out),
    .Q(PC_JUMP_OP_q), .clr(and_1_out));
  Multiplexer #(.width(24)) multiplexer_3 (
    .in0(START_DIR_q), .in1(END_DIR_q), .out(multiplexer_3_out), .sel(comparator_4_eq));
  Hex_Digit_Display hex_digit_display_35 (.value(binary_to_bcd_converter_9_p5));  // open: dp
  Multiplexer #(.width(10)) multiplexer_4 (
    .in0(GPU_PC_q_2), .in1(GPU_INS_ADR_q), .out(multiplexer_4_out), .sel(demultiplexer_1_out10));
  Multiplexer #(.select(2), .width(24)) multiplexer_5 (
    .in0(multiplexer_2_out), .in1(STACK_PC_dout), .in2(multiplexer_3_out), .out(multiplexer_5_out),
    .sel(PC_JUMP_OP_q));  // open: in3
  Hex_Digit_Display hex_digit_display_36 (.value(binary_to_bcd_converter_9_p6));  // open: dp
  RAM #(.addrWidth(10), .dataWidth(7)) GPU_INSTRUCTION (
    .addr(multiplexer_4_out), .we(ram_load_read_controller_2_store), .oe(ram_load_read_controller_2_load),
    .clk(clock_2_out), .din(multiplexer_2_out[6:0]));  // open: dout
  RAM_LOAD_READ_CONTROLLER ram_load_read_controller_2 (
    .STORE_SIGNAL(demultiplexer_1_out10), .LOAD(ram_load_read_controller_2_load),
    .STORE(ram_load_read_controller_2_store));
  Clock clock_2 (.out(clock_2_out));
  ROM #(.dataWidth(24)) ColorPalette (.addr(in_1), .data(ColorPalette_data));
  Counter #(.max('hffff), .width(16)) GPU_PC (
    .Q({GPU_PC_q_2[9:5], GPU_PC_q[10:8], GPU_PC_q_2[4:0], GPU_PC_q[2:0]}), .up(1'b1), .clk(clock_2_out),
    .clr(and_1_out));  // open: load, D, count, carry
  Demultiplexer #(.width(16)) demultiplexer_2 (
    .in({GPU_PC_q_2[9:5], GPU_PC_q[10:8], GPU_PC_q_2[4:0], GPU_PC_q[2:0]}), .sel(counter_1_q));  // open: out0, out1
  Demultiplexer #(.width(24)) demultiplexer_3 (
    .out0(demultiplexer_3_out0), .out1(demultiplexer_3_out1), .in(ColorPalette_data), .sel(not_4_out));
  RAM_LOAD_READ_CONTROLLER ram_load_read_controller_3 (
    .STORE_SIGNAL(counter_1_q), .LOAD(ram_load_read_controller_3_load),
    .STORE(ram_load_read_controller_3_store));
  RAM_LOAD_READ_CONTROLLER ram_load_read_controller_4 (
    .STORE_SIGNAL(not_4_out), .LOAD(ram_load_read_controller_4_load), .STORE(ram_load_read_controller_4_store));
  not not_4 (not_4_out, counter_1_q);
  // RGB_Video #(.cursor("No Cursor"), .height(256), .reset("Synchronous"), .width(256)) rgb_video_1: pin names not known; wires that end beside it: and_1_out, clock_2_out, 1'b1, {GPU_PC_q_2[4:0], GPU_PC_q[2:0]}, {GPU_PC_q_2[9:5], GPU_PC_q[10:8]}, rgb_video_1_p6
  RAM #(.addrWidth(16), .dataWidth(24)) FrameBuffer0 (
    .addr({GPU_PC_q_2[9:5], GPU_PC_q[10:8], GPU_PC_q_2[4:0], GPU_PC_q[2:0]}),
    .we(ram_load_read_controller_3_store), .oe(ram_load_read_controller_3_load), .clk(clock_2_out),
    .din(demultiplexer_3_out0), .dout(FrameBuffer0_dout));
  RAM #(.addrWidth(16), .dataWidth(24)) FrameBuffer1 (
    .addr({GPU_PC_q_2[9:5], GPU_PC_q[10:8], GPU_PC_q_2[4:0], GPU_PC_q[2:0]}),
    .we(ram_load_read_controller_4_store), .oe(ram_load_read_controller_4_load), .clk(clock_2_out),
    .din(demultiplexer_3_out1), .dout(FrameBuffer1_dout));
  D_Flip_Flop d_ff_2 (.D(Frame_Ready_out), .clk(clock_2_out), .Q(d_ff_2_q));  // open: Qn, preset, reset
  Button Frame_Ready (.out(Frame_Ready_out));
  not not_5 (not_5_out, d_ff_2_q);
  S_R_Flip_Flop s_r_ff_1 (.S(and_4_out), .clk(clock_2_out), .R(and_5_out), .Q(s_r_ff_1_q));  // open: Qn, preset, reset
  and and_4 (and_4_out, Frame_Ready_out, not_5_out);
  Comparator #(.mode("unsigned"), .width(16)) comparator_5 (
    .a({GPU_PC_q_2[9:5], GPU_PC_q[10:8], GPU_PC_q_2[4:0], GPU_PC_q[2:0]}), .b({16{1'b1}}),
    .eq(comparator_5_eq));  // open: gt, lt
  and and_5 (and_5_out, comparator_5_eq, s_r_ff_1_q);
  Multiplexer #(.width(24)) multiplexer_6 (
    .in0(FrameBuffer0_dout), .in1(FrameBuffer1_dout), .out(rgb_video_1_p6), .sel(counter_1_q));
  Counter #(.max('h1), .width(1)) counter_1 (
    .count(and_5_out), .Q(counter_1_q), .up(1'b1), .clk(clock_2_out), .clr(and_1_out));  // open: load, D, carry

  // Notes on the sheet:
  //   Y
  //   X
  //   contents of Instructions (hex, n*v repeats v):
  //   25900000000 1590000004c 25900000001 15900000012 25900000002 15900000031 25900000003 15900000020
  //   25900000004 15900000000 25900000005 1590000001f 25900000006 15900000020 25900000007 1590000002f
  //   25900000008 15900000020 25900000009 1590000001c 2590000000a 15900000000 2590000000b 1590000002e
  //   2590000000c 15900000020 2590000000d 1590000001c 2590000000e 15900000027 2590000000f 15900000024
  //   25900000010 15900000036 25900000011 1590000001c 25900000012 1590000002e 25900000013 1590000004b
  //   1900000100 3900000008 21900000003
  //   R
  //   contents of ColorPalette (hex, n*v repeats v):
  //   0 ffffff ff ff00 ff0000
endmodule

module RAM_LOAD_READ_CONTROLLER (
  input  STORE_SIGNAL,
  output LOAD,
  output STORE
);

  Demultiplexer demultiplexer_1 (.out0(LOAD), .out1(STORE), .in(1'b1), .sel(STORE_SIGNAL));
endmodule
